# Fritzing sketch schematic diagram (saved by Fritzing 0.9.3b)

parts:
  MH-ET_LIVE_ESP32_DEVKIT1 = MH-ET LIVE ESP32 DEVKIT 38 pins
  HC-SR04_Sensor_1 = HC-SR04 Ultrasonic Distance Sensor
  J1 = Basic Servo
  A1 = DHT22 module
  Part1 = HC-SR501 Body Sensor Module
  ZS-042_RTC1 = ZS-042 RTC Module
  SIM800L_BO1 = SIM800L BO
  LCD1 = 1_7in tft lcd

nets:
  N1: MH-ET_LIVE_ESP32_DEVKIT1.3V3, LCD1.pin_8, LCD1.pin_9
  N2: MH-ET_LIVE_ESP32_DEVKIT1.IO27, Part1.OUT
  N3: MH-ET_LIVE_ESP32_DEVKIT1.IO14, HC-SR04_Sensor_1.TRIG, HC-SR04_Sensor_1.ECHO
  GND: MH-ET_LIVE_ESP32_DEVKIT1.GND#58, HC-SR04_Sensor_1.GND, J1.gnd, A1.-, Part1.GND, ZS-042_RTC1.GND
  N4: MH-ET_LIVE_ESP32_DEVKIT1.IO13, A1.Out
  VCC: MH-ET_LIVE_ESP32_DEVKIT1.5V, HC-SR04_Sensor_1.VCC, J1.vcc, A1.+, Part1.VCC, ZS-042_RTC1.VCC, SIM800L_BO1.PIN1, LCD1.pin2
  N5: MH-ET_LIVE_ESP32_DEVKIT1.GND#64, SIM800L_BO1.pin_6, LCD1.pin_1, LCD1.pin_14
  N6: MH-ET_LIVE_ESP32_DEVKIT1.IO23, LCD1.pin4
  N7: MH-ET_LIVE_ESP32_DEVKIT1.IO22, ZS-042_RTC1.SCL
  N8: MH-ET_LIVE_ESP32_DEVKIT1.IO21, ZS-042_RTC1.SDA
  N9: MH-ET_LIVE_ESP32_DEVKIT1.IO19, J1.pulse
  N10: MH-ET_LIVE_ESP32_DEVKIT1.IO18, LCD1.pin3
  N11: MH-ET_LIVE_ESP32_DEVKIT1.IO17, SIM800L_BO1.pin_4
  N12: MH-ET_LIVE_ESP32_DEVKIT1.IO16, SIM800L_BO1.pin_5
  N13: MH-ET_LIVE_ESP32_DEVKIT1.IO4, LCD1.pin_5
  N14: MH-ET_LIVE_ESP32_DEVKIT1.IO2, LCD1.pin_6
  N15: MH-ET_LIVE_ESP32_DEVKIT1.IO15, LCD1.pin_7

custom parts:
  MH-ET LIVE ESP32 DEVKIT 38 pins: http://mh.nodebb.com/topic/2/mh-et-live-esp32-devkit
  DHT22 module: DHT22 module. Pins VCC Data GND.
  HC-SR501 Body Sensor Module: Pyroelectric Infrared PIR Motion Sensor Detector Module
  1_7in tft lcd: This is the Zoll 1.77in spi lcd display. The 1.77" display has 128x160 color pixels.
